// Logisim project t888.circ as structural Verilog: 4 circuits, main circuit t888
module t888 (
  input  [7:0] in_1,
  input  [7:0] in_2,
  input  in_3,
  input  in_4,
  input  in_5,
  input  in_6
);

  wire undriven;

  ALU alu_1 ();  // open: OpSel, DataBus, clk, clr, carry_en, carry_mode, Rout, ALUen, DataBus_2, State
  // Probe on in_2
  RAM #(.Select("low")) ram_1 (.addr(in_1), .data(in_2), .sel(undriven), .clk(in_4), .ld(in_5), .clr(in_6));
endmodule

module ALU (
  input  [3:0] OpSel,
  input  [7:0] DataBus,
  input  clk,
  input  clr,
  input  carry_en,
  input  carry_mode,
  input  Rout,
  input  ALUen,
  output [7:0] DataBus_2,
  output [1:0] State
);

  wire adder_2_cout, and_4_out, and_5_out, C_en_q, multiplexer_2_out, not_2_out, subtractor_2_bout,
       subtractor_3_bout, zerotest_1_iszero;
  wire [0:0] and_3_out;
  wire [7:0] Accum_q, adder_1_out, adder_2_out, and_1_out, and_2_out, Data_q, multiplexer_1_out,
       multiplexer_3_out, negator_1_out, not_1_out, or_1_out, subtractor_1_out, subtractor_2_out,
       subtractor_3_out, xor_1_out;

  Adder adder_1 (.a(Accum_q), .b(8'h1), .out(adder_1_out));  // open: cin, cout
  Subtractor subtractor_1 (.a(Accum_q), .b(8'h1), .out(subtractor_1_out));  // open: bin, bout
  Negator negator_1 (.in(Accum_q), .out(negator_1_out));
  assign not_1_out = ~Accum_q;  // NOT_Gate not_1, 8 bits wide
  Multiplexer #(.width(8), .enable("false")) multiplexer_1 (
    .in0(Data_q), .in1(Accum_q), .out(multiplexer_1_out), .sel(Rout));
  Adder adder_2 (.a(Accum_q), .b(Data_q), .out(adder_2_out), .cin(and_3_out[0]), .cout(adder_2_cout));
  Subtractor subtractor_2 (
    .a(Accum_q), .b(Data_q), .out(subtractor_2_out), .bin(and_3_out[0]), .bout(subtractor_2_bout));
  Subtractor subtractor_3 (
    .a(Data_q), .b(Accum_q), .out(subtractor_3_out), .bin(and_3_out[0]), .bout(subtractor_3_bout));
  assign and_1_out = Accum_q & Data_q;  // AND_Gate and_1, 8 bits wide
  assign and_2_out = Accum_q & ~Data_q;  // AND_Gate and_2, 8 bits wide
  assign or_1_out = Accum_q | Data_q;  // OR_Gate or_1, 8 bits wide
  assign xor_1_out = Accum_q ^ Data_q;  // XOR_Gate xor_1, 8 bits wide
  not not_2 (not_2_out, OpSel[2]);
  Register #(.trigger("low"), .Select("low")) Data (.D(DataBus), .Q(Data_q), .clk(carry_en), .clr(clr));  // open: en
  Multiplexer #(.select(3)) multiplexer_2 (
    .in1(adder_2_cout), .in2(subtractor_2_bout), .in3(subtractor_3_bout), .in5(Accum_q[7]), .in6(Accum_q[0]),
    .in7(Accum_q[0]), .out(multiplexer_2_out), .sel({OpSel[3], OpSel[1:0]}), .en(not_2_out));  // open: in0, in4
  and and_3 (and_3_out[0], State[1], C_en_q);
  Register #(.width(1), .Select("high")) Carry (
    .D(multiplexer_2_out), .Q(State[1]), .clk(carry_en), .clr(carry_mode));  // open: en
  Register #(.width(1), .Select("high")) C_en (.D(carry_en), .en(carry_mode), .Q(C_en_q), .clk(carry_en), .clr(clr));
  and and_4 (and_4_out, Rout, ALUen);
  Multiplexer #(.select(4), .width(8), .enable("false")) multiplexer_3 (
    .in0({8{1'b0}}), .in1({Accum_q[6:0], and_3_out[0]}), .in2({and_3_out[0], Accum_q[7:1]}),
    .in3({{2{Accum_q[7]}}, Accum_q[6:1]}), .in4(adder_1_out), .in5(subtractor_1_out), .in6(negator_1_out),
    .in7(not_1_out), .in8(multiplexer_1_out), .in9(adder_2_out), .in10(subtractor_2_out),
    .in11(subtractor_3_out), .in12(and_1_out), .in13(and_2_out), .in14(or_1_out), .in15(xor_1_out),
    .out(multiplexer_3_out), .sel(OpSel));
  Register #(.Select("low")) Accum (.D(multiplexer_3_out), .en(and_4_out), .Q(Accum_q), .clk(carry_en), .clr(clr));
  assign DataBus_2 = and_5_out ? multiplexer_3_out : 8'bz;  // Controlled_Buffer controlled_buffer_1
  and and_5 (and_5_out, ALUen, ~Rout, ~carry_en);  // AND_Gate
  ZeroTest zerotest_1 (.Input(multiplexer_3_out), .IsZero(zerotest_1_iszero));
  Register #(.width(1), .Select("high")) Zero (
    .D(zerotest_1_iszero), .en(ALUen), .Q(State[0]), .clk(carry_en), .clr(clr));

  assign clk = carry_en;

  // Notes on the sheet:
  //   DataBus: pull=down
endmodule

module ZeroTest (
  input  [7:0] Input,
  output IsZero
);

  nor nor_1 (IsZero, Input[0], Input[1], Input[2], Input[3], Input[4], Input[5], Input[6], Input[7]);

  // Notes on the sheet:
  //   Input: pull=up
endmodule

module ValueSwap (
  input  [7:0] in_1,
  input  [7:0] in_2,
  input  in_3,
  output [7:0] out_4,
  output [7:0] out_5
);

  Multiplexer #(.width(8), .enable("false")) multiplexer_1 (.in0(in_1), .in1(in_2), .out(out_4), .sel(in_3));
  Multiplexer #(.width(8), .enable("false")) multiplexer_2 (.in0(in_2), .in1(in_1), .out(out_5), .sel(in_3));
  Pull_Resistor pull_resistor_1 (.node(in_3));
endmodule
